// Logisim project Trabalho_Final_CD_Logisim.circ as structural Verilog: 1 circuit, main circuit main
module main (
  input  A1,
  input  B1,
  input  C1,
  input  D1,
  input  A2,
  input  B2,
  input  C2,
  input  D2,
  input  ALVOA,
  input  ALVOB,
  input  ALVOC,
  input  ALVOD,
  output S11,
  output S12,
  output S13,
  output SF_ACERTOU,
  output S14,
  output SF_ERROU,
  output S21,
  output S22,
  output S23,
  output S24
);

  wire and_1_out, and_2_out, and_3_out, and_4_out, and_5_out, and_6_out, and_7_out, and_8_out, and_9_out,
       and_10_out, and_11_out, and_12_out, and_13_out, and_14_out, and_15_out, and_16_out, and_17_out,
       and_18_out, and_19_out, and_20_out, and_21_out, and_22_out, and_23_out, and_24_out, and_25_out,
       and_26_out, and_27_out, and_28_out, and_29_out, and_30_out, and_31_out, and_32_out, DISPARAR_out,
       nor_1_out, not_1_out, not_2_out, not_3_out, not_4_out, not_5_out, not_6_out, not_7_out, not_8_out,
       xnor_1_out, xnor_2_out, xnor_3_out, xnor_4_out, xnor_5_out, xnor_6_out, xnor_7_out, xnor_8_out;

  Button DISPARAR (.out(DISPARAR_out));
  not not_1 (not_1_out, A1);
  not not_2 (not_2_out, B1);
  not not_3 (not_3_out, C1);
  not not_4 (not_4_out, D1);
  not not_5 (not_5_out, A2);
  not not_6 (not_6_out, B2);
  not not_7 (not_7_out, C2);
  not not_8 (not_8_out, D2);
  and and_1 (and_1_out, C1, D1);
  and and_2 (and_2_out, B1, not_3_out, not_4_out);
  and and_3 (and_3_out, A1, B1);
  and and_4 (and_4_out, not_1_out, not_3_out);
  and and_5 (and_5_out, B1, C1, not_4_out);
  and and_6 (and_6_out, A1, C1, D1);
  and and_7 (and_7_out, not_3_out, not_4_out);
  and and_8 (and_8_out, not_1_out, not_2_out, C1, D1);
  and and_9 (and_9_out, not_1_out, B1, not_3_out);
  and and_10 (and_10_out, A1, not_4_out);
  and and_11 (and_11_out, not_1_out, not_2_out, not_3_out);
  and and_12 (and_12_out, not_1_out, not_2_out, not_4_out);
  and and_13 (and_13_out, not_3_out, not_4_out);
  and and_14 (and_14_out, not_1_out, B1, C1, D1);
  and and_15 (and_15_out, A1, not_2_out, C1, D1);
  and and_16 (and_16_out, C2, D2);
  and and_17 (and_17_out, B2, not_7_out, not_8_out);
  and and_18 (and_18_out, A2, B2);
  and and_19 (and_19_out, not_5_out, not_7_out);
  and and_20 (and_20_out, B2, C2, not_8_out);
  and and_21 (and_21_out, A2, C2, D2);
  and and_22 (and_22_out, not_7_out, not_8_out);
  and and_23 (and_23_out, not_5_out, not_6_out, C2, D2);
  and and_24 (and_24_out, not_5_out, B2, not_7_out);
  and and_25 (and_25_out, A2, not_8_out);
  and and_26 (and_26_out, not_5_out, not_6_out, not_7_out);
  and and_27 (and_27_out, not_5_out, not_6_out, not_8_out);
  and and_28 (and_28_out, not_7_out, not_8_out);
  and and_29 (and_29_out, not_5_out, B2, C2, D2);
  and and_30 (and_30_out, A2, not_6_out, C2, D2);
  or or_1 (S11, and_1_out, and_2_out, and_3_out);
  or or_2 (S12, and_4_out, and_5_out, and_6_out);
  or or_3 (S13, and_7_out, and_8_out, and_9_out, and_10_out);
  or or_4 (S14, and_11_out, and_12_out, and_13_out, and_14_out, and_15_out);
  or or_5 (S21, and_16_out, and_17_out, and_18_out);
  or or_6 (S22, and_19_out, and_20_out, and_21_out);
  or or_7 (S23, and_22_out, and_23_out, and_24_out, and_25_out);
  or or_8 (S24, and_26_out, and_27_out, and_28_out, and_29_out, and_30_out);
  xnor xnor_1 (xnor_1_out, S11, ALVOA);
  xnor xnor_2 (xnor_2_out, S12, ALVOB);
  xnor xnor_3 (xnor_3_out, S13, ALVOC);
  xnor xnor_4 (xnor_4_out, S14, ALVOD);
  xnor xnor_5 (xnor_5_out, S21, ALVOA);
  xnor xnor_6 (xnor_6_out, S22, ALVOB);
  xnor xnor_7 (xnor_7_out, S23, ALVOC);
  xnor xnor_8 (xnor_8_out, S24, ALVOD);
  and and_31 (and_31_out, xnor_5_out, xnor_6_out, xnor_7_out, xnor_8_out, DISPARAR_out);
  and and_32 (and_32_out, xnor_1_out, xnor_2_out, xnor_3_out, xnor_4_out, DISPARAR_out);
  nor nor_1 (nor_1_out, and_32_out, and_31_out);
  or or_9 (SF_ACERTOU, and_32_out, and_31_out);
  and and_33 (SF_ERROU, nor_1_out, DISPARAR_out);
endmodule
